// Digital circuit front.dig as structural Verilog
module front (
  input  [15:0] A,
  input  [7:0] SD,
  output [15:0] R0,
  output [15:0] R1,
  output [15:0] R2,
  output [15:0] R3,
  output [15:0] B,
  output [1:0] rs,
  output [15:0] A_2,
  output [15:0] B_2,
  output [1:0] rd
);

  wire button_1_out, button_2_out;
  wire [1:0] PC_out;
  wire [15:0] execute_1_sum;
  wire [31:0] Program_d;

  Button button_1 (.out(button_1_out));
  EEPROMDualPort #(.Bits(32)) Program (
    .A(PC_out), .Din({{8{1'b0}}, SD, A}), .str(1'b1), .C(button_1_out), .ld(1'b1), .D(Program_d));
  Counter #(.Bits(2)) PC (.en(1'b1), .C(button_2_out), .clr(1'b0), .out(PC_out));  // open: ovf
  Button button_2 (.out(button_2_out));
  decoder decoder_1 (.i(Program_d), .A(A_2), .rs(rs), .rd(rd));
  execute execute_1 (.A(A_2), .B(B), .sum(execute_1_sum));
  regfile regfile_1 (.rs(rs), .rd(rd), .D(execute_1_sum), .CL(button_2_out), .R0(B), .R1(R0), .R2(R1), .R3(R2), .B(R3));

  assign B_2 = B;

  // Other names for the same wires on the sheet: A_t[15:0] = A_2

  // Notes on the sheet:
  //   A: default 100
  //   SD: default 1
  //   contents of Program (hex, n*v repeats v):
  //   10064,1200c8,230063,300022
endmodule
